# Fritzing sketch waveform (saved by Fritzing 0.9.3b)
breadboards: 1

parts:
  Part1 = Arduino Nano (Rev3.0) (ICSP)
  U1 = AD9835 [package=tssop16]
  WeMos_D1_Mini_OLED_Shield1 = WeMos D1 Mini OLED Shield
  RE1 = Rotary Encoder [package=THT]
  U2 = LM358 [package=dip08]
  R1 = Resistor [tolerance=±5% resistance=3k package="2010 [SMD]"]
  R2 = Resistor [tolerance=±5% resistance=1.5k package="2010 [SMD]"]
  R3 = Resistor [tolerance=±5% resistance=4.7k package="2010 [SMD]"]
  R4 = Resistor [tolerance=±5% resistance=3.7k package="2010 [SMD]"]

nets:
  N1: Part1.D2, RE1.EncoderPinB
  N2: Part1.D3, RE1.EncoderPinA
  N3: Part1.D5, U1.FSYNC
  N4: Part1.D8, WeMos_D1_Mini_OLED_Shield1.D5
  N5: Part1.D9, WeMos_D1_Mini_OLED_Shield1.A0
  N6: Part1.D10, WeMos_D1_Mini_OLED_Shield1.RST
  N7: Part1.D13/SCK, U1.SCLK, WeMos_D1_Mini_OLED_Shield1.D0
  N8: Part1.D11/MOSI, U1.SDATA, WeMos_D1_Mini_OLED_Shield1.D1
  N9: WeMos_D1_Mini_OLED_Shield1.TX, U2.G$1_+IN
  GND: RE1.EncoderPinC, R2.Pin_0, R4.Pin_1
  N10: U2.G$1_OUT, U2.G$2_+IN, R1.Pin_1
  N11: U2.G$1_-IN, R2.Pin_1
  N12: U2.G$2_-IN, R3.Pin_0, R4.Pin_0
  N13: U2.G$2_OUT, R3.Pin_1
